# Fritzing sketch smartroomcontroller (saved by Fritzing 0.9.4)
breadboards: 1

parts:
  RG_encoder1 = SprkFn RG Encoder [package="DIP (Dual Inline) [THT]"]
  WS2812B1 = WS2812B NP [package="DIP (Dual Inline) [THT]"]
  HC-SR04_Sensor_1 = HC-SR04 Ultrasonic Distance Sensor
  S1 = Pushbutton [package="[THT]"]
  R1 = Resistor [tolerance=±5% resistance=220 package="2512 [SMD]"]
  R2 = Resistor [tolerance=±5% resistance=220 package="2512 [SMD]"]
  R3 = Resistor [tolerance=±5% resistance=220 package="2512 [SMD]"]
  R4 = Resistor [tolerance=±5% resistance=220 package="2512 [SMD]"]
  M1 = BMP280
  S5 = Pushbutton [package="[THT]"]
  S6 = Pushbutton [package="[THT]"]
  S7 = Pushbutton [package="[THT]"]
  WIZ820io1 = WIZ820io [part_number=WIZ820io]
  OLED_I2C1 = OLED 128x64 I2C Monochrome Display
  Teensy_3_1 = Teensy 3.1
  C1 = Capacitor [package=cap-pth-small2]
  C2 = Capacitor [package=cap-pth-small2]

nets (from the schematic view):
  N1: RG_encoder1.+R, Teensy_3_1.A3/D17
  N2: RG_encoder1.+G, Teensy_3_1.A1/D15
  N3: RG_encoder1.SW, Teensy_3_1.A2/D16
  GND: RG_encoder1.GND, RG_encoder1.C, WS2812B1.GND, HC-SR04_Sensor_1.ECHO, HC-SR04_Sensor_1.GND, R1.Pin_1, R2.Pin_1, R3.Pin_1, R4.Pin_1, M1.GND, WIZ820io1.GND, OLED_I2C1.GND, Teensy_3_1.GND, Teensy_3_1.D2, C1.1, C2.1
  N4: RG_encoder1.A, Teensy_3_1.D8, C1.2
  N5: RG_encoder1.B, Teensy_3_1.D7, C2.2
  VIN: WS2812B1.5V, HC-SR04_Sensor_1.VCC, S1.Pin_3, S1.Pin_4, M1.VIN, S5.Pin_3, S5.Pin_4, S6.Pin_3, S6.Pin_4, S7.Pin_3, S7.Pin_4, WIZ820io1.VIN, OLED_I2C1.VDD, Teensy_3_1.3V3
  N6: WS2812B1.DI, Teensy_3_1.D0
  N7: HC-SR04_Sensor_1.TRIG, Teensy_3_1.D3
  N8: S1.Pin_1, S1.Pin_2, R4.Pin_0, Teensy_3_1.A9/D23
  N9: R1.Pin_0, S7.Pin_1, S7.Pin_2, Teensy_3_1.A6/D20
  N10: R2.Pin_0, S6.Pin_1, S6.Pin_2, Teensy_3_1.A7/D21
  N11: R3.Pin_0, S5.Pin_1, S5.Pin_2, Teensy_3_1.A8/D22
  N12: M1.SCL, OLED_I2C1.SCK, Teensy_3_1.A5/D19
  N13: M1.SDA, OLED_I2C1.SDA, Teensy_3_1.A4/D18
  N14: WIZ820io1.MOSI, Teensy_3_1.D11
  N15: WIZ820io1.SCLK, Teensy_3_1.D13
  N16: WIZ820io1.nSS, Teensy_3_1.D10
  N17: WIZ820io1.MISO, Teensy_3_1.D12
  N18: WIZ820io1.nRESET, Teensy_3_1.D9

custom parts:
  SprkFn RG Encoder: SparkFun RG Rotary Encoder
  WS2812B NP: WS2812B Adafruit Breakout Neopixel
  Pushbutton: A generic pushbutton.
  BMP280: Temperature Humidity Barometric presure Sensor, I2C
  Pushbutton: A generic pushbutton.
  Pushbutton: A generic pushbutton.
  Pushbutton: A generic pushbutton.
